// Digital circuit alu.dig as structural Verilog
module alu (
  input  [31:0] A,
  input  [31:0] B,
  input  [1:0] ALUOp,
  output [31:0] R,
  output N,
  output Z,
  output C,
  output V,
  output [3:0] NZCV
);

  wire and_1_out, and_2_out, and_3_out, and_4_out, comparator_1_gt, comparator_2_lt, comparator_3_lt,
       comparator_4_gt, comparator_5_lt, comparator_6_gt;
  wire [31:0] add_1_s, sub_1_s;
  wire [63:0] mul_1_mul;

  Add #(.Bits(32)) add_1 (.a(A), .b(B), .c_i(1'b0), .s(add_1_s));  // open: c_o
  Sub #(.Bits(32)) sub_1 (.a(A), .b(B), .c_i(1'b0), .s(sub_1_s));  // open: c_o
  Mul #(.Bits(32)) mul_1 (.a(A), .b(B), .mul(mul_1_mul));
  Comparator #(.Signed("true"), .Bits(32)) comparator_1 (.a(A), .b({32{1'b0}}), .gt(comparator_1_gt));  // open: eq, lt
  Comparator #(.Signed("true"), .Bits(32)) comparator_2 (.a(B), .b({32{1'b0}}), .lt(comparator_2_lt));  // open: gt, eq
  Comparator #(.Signed("true"), .Bits(32)) comparator_3 (.a(A), .b({32{1'b0}}), .lt(comparator_3_lt));  // open: gt, eq
  Comparator #(.Signed("true"), .Bits(32)) comparator_4 (.a(B), .b({32{1'b0}}), .gt(comparator_4_gt));  // open: eq, lt
  Multiplexer #(.Selector_Bits(2), .Bits(32)) multiplexer_1 (
    .sel(ALUOp), .in_0(add_1_s), .in_1(sub_1_s), .in_2(mul_1_mul[31:0]), .in_3(B), .out({N, R[30:0]}));
  and and_1 (and_1_out, comparator_1_gt, comparator_2_lt);
  Comparator #(.Signed("true"), .Bits(32)) comparator_5 (
    .a({N, R[30:0]}), .b({32{1'b0}}), .lt(comparator_5_lt));  // open: gt, eq
  and and_2 (and_2_out, comparator_3_lt, comparator_4_gt);
  Comparator #(.Signed("true"), .Bits(32)) comparator_6 (
    .a({N, R[30:0]}), .b({32{1'b0}}), .gt(comparator_6_gt));  // open: eq, lt
  Comparator #(.Bits(32)) Z_flag (.a({N, R[30:0]}), .b({32{1'b0}}), .eq(NZCV[1]));  // open: gt, lt
  Comparator #(.Bits(32)) C_flag (.a(B), .b(A), .gt(C));  // open: eq, lt
  and and_3 (and_3_out, and_1_out, comparator_5_lt);
  and and_4 (and_4_out, and_2_out, comparator_6_gt);
  or or_1 (NZCV[3], and_3_out, and_4_out);

  assign {NZCV[2], NZCV[0]} = {C, N};
  assign R[31] = N;
  assign V = NZCV[3];
  assign Z = NZCV[1];
endmodule
