// Digital circuit control.dig as structural Verilog
module control (
  input  [31:0] iw,
  input  [3:0] NZCV,
  input  CLK,
  output RFW,
  output [1:0] EXT,
  output [1:0] ALUop,
  output ALU1src,
  output MUL,
  output LDR,
  output STR,
  output CMP,
  output BR,
  output BX,
  output BL
);

  wire AL, and_1_out, BR_cond, BR_t, C, comparator_4_eq, comparator_5_eq, comparator_6_eq, comparator_7_eq,
       comparator_8_eq, EQ, GE, GT, N, NE, nv, V, Z, z1;

  Comparator comparator_1 (.a(N), .b(V), .eq(nv));  // open: gt, lt
  Comparator comparator_2 (.a(Z), .b(1'b1), .eq(z1));  // open: gt, lt
  Comparator #(.Bits(4)) comparator_3 (.a(iw[31:28]), .b(4'b1110), .eq(AL));  // open: gt, lt
  main_decoder main_decoder_1 (
    .iw(iw), .RFW(RFW), .EXT(EXT), .ALUop(ALUop), .ALU1src(ALU1src), .CMP(CMP), .MUL(MUL), .LDR(LDR),
    .STR(STR), .BR(BR_t), .BL(BL), .BX(BX));
  Register #(.Bits(4)) CPSR (.D(NZCV), .C(CLK), .en(CMP), .Q({V, C, Z, N}));
  Comparator #(.Bits(4)) comparator_4 (.a(iw[31:28]), .b(4'b0000), .eq(comparator_4_eq));  // open: gt, lt
  Comparator #(.Bits(4)) comparator_5 (.a(iw[31:28]), .b(4'b0001), .eq(comparator_5_eq));  // open: gt, lt
  Comparator #(.Bits(4)) comparator_6 (.a(iw[31:28]), .b(4'b1100), .eq(comparator_6_eq));  // open: gt, lt
  Comparator comparator_7 (.a(1'b0), .b(Z), .eq(comparator_7_eq));  // open: gt, lt
  Comparator #(.Bits(4)) comparator_8 (.a(iw[31:28]), .b(4'b1010), .eq(comparator_8_eq));  // open: gt, lt
  and and_1 (and_1_out, comparator_7_eq, nv);
  and and_2 (EQ, comparator_4_eq, z1);
  and and_3 (NE, comparator_5_eq, ~z1);  // And
  and and_4 (GT, comparator_6_eq, and_1_out);
  and and_5 (GE, comparator_8_eq, nv);
  or or_1 (BR_cond, EQ, NE, GT, GE, AL);
  and and_6 (BR, BR_t, BR_cond);

  // Notes on the sheet:
  //   EQ
  //   NE
  //   GT
  //   GE
  //   AL
endmodule
