// Digital circuit inst_mem.dig as structural Verilog
module inst_mem (
  input  [6:0] A,
  input  [2:0] Sel,
  output [31:0] D
);

  wire [31:0] fib_iter_10_d, fib_iter_19_d, fib_rec_10_d, fib_rec_19_d, find_max_d, quadratic_d,
       simple_sort_d, sum_array_d;

  ROM #(.AddrBits(7), .Bits(32)) quadratic (.A(A), .sel(1'b1), .D(quadratic_d));
  ROM #(.AddrBits(7), .Bits(32)) sum_array (.A(A), .sel(1'b1), .D(sum_array_d));
  ROM #(.AddrBits(7), .Bits(32)) find_max (.A(A), .sel(1'b1), .D(find_max_d));
  ROM #(.AddrBits(7), .Bits(32)) fib_iter_10 (.A(A), .sel(1'b1), .D(fib_iter_10_d));
  ROM #(.AddrBits(7), .Bits(32)) fib_iter_19 (.A(A), .sel(1'b1), .D(fib_iter_19_d));
  ROM #(.AddrBits(7), .Bits(32)) fib_rec_10 (.A(A), .sel(1'b1), .D(fib_rec_10_d));
  ROM #(.AddrBits(7), .Bits(32)) fib_rec_19 (.A(A), .sel(1'b1), .D(fib_rec_19_d));
  ROM #(.AddrBits(7), .Bits(32)) simple_sort (.A(A), .sel(1'b1), .D(simple_sort_d));
  Multiplexer #(.Selector_Bits(3), .Bits(32)) multiplexer_1 (
    .sel(Sel), .in_0(quadratic_d), .in_1(sum_array_d), .in_2(find_max_d), .in_3(fib_iter_10_d),
    .in_4(fib_iter_19_d), .in_5(fib_rec_10_d), .in_6(fib_rec_19_d), .in_7(simple_sort_d), .out(D));

  // Notes on the sheet:
  //   contents of quadratic (hex, n*v repeats v):
  //   e3a00002,e3a01003,e3a02004,e3a03005,eb000000,eafffffe,e0020290,e1a0c000,e000009c,
  //   e0000091,e0820000,e0830000,e12fff1e
  //   contents of sum_array (hex, n*v repeats v):
  //   e3a0d080,e3a00020,e00d0d90,e24dd018,e3a00001,e58d0000,e3a00002,e58d0004,e3a00003,
  //   e58d0008,e3a00004,e58d000c,e3a00006,e58d0010,e1a0000d,e3a01005,eb000000,eafffffe,
  //   e3a02000,e3a03000,e1520001,a000004,e590c000,e083300c,e2822001,e2800004,eafffff8,e1a00003,
  //   e12fff1e
  //   contents of find_max (hex, n*v repeats v):
  //   e3a0d080,e3a00020,e00d0d90,e24dd018,e3a00003,e58d0000,e3a00006,e58d0004,e3a00001,
  //   e58d0008,e3a00008,e58d000c,e3a00004,e58d0010,e1a0000d,e3a01005,eb000000,eafffffe,
  //   e3a03000,e5902000,e2800004,e2833001,e1530001,a000004,e590c000,e152000c,aafffff8,e1a0200c,
  //   eafffff6,e1a00002,e12fff1e
  //   contents of fib_iter_10 (hex, n*v repeats v):
  //   e3a0000a,eb000000,eafffffe,e3500000,a000009,e3a01001,e3a02000,e3a03001,e1510000,a000005,
  //   e082c003,e1a02003,e1a0300c,e2811001,eafffff8,e3a03000,e1a00003,e12fff1e
  //   contents of fib_iter_19 (hex, n*v repeats v):
  //   e3a00013,eb000000,eafffffe,e3500000,a000009,e3a01001,e3a02000,e3a03001,e1510000,a000005,
  //   e082c003,e1a02003,e1a0300c,e2811001,eafffff8,e3a03000,e1a00003,e12fff1e
  //   contents of fib_rec_10 (hex, n*v repeats v):
  //   e3a0d080,e3a00020,e00d0d90,e3a0000a,eb000000,eafffffe,e3a03001,e1530000,aa00000c,
  //   e24dd010,e58de000,e58d0004,e2400001,ebfffff7,e58d0008,e59d0004,e2400002,ebfffff3,
  //   e59d1008,e0800001,e59de000,e28dd010,e12fff1e
  //   contents of fib_rec_19 (hex, n*v repeats v):
  //   e3a0d080,e3a00020,e00d0d90,e3a00013,eb000000,eafffffe,e3a03001,e1530000,aa00000c,
  //   e24dd010,e58de000,e58d0004,e2400001,ebfffff7,e58d0008,e59d0004,e2400002,ebfffff3,
  //   e59d1008,e0800001,e59de000,e28dd010,e12fff1e
  //   contents of simple_sort (hex, n*v repeats v):
  //   e3a0d080,e3a00020,e00d0d90,e24dd018,e3a00001,e58d0000,e3a00004,e58d0004,e3a00007,
  //   e58d0008,e3a00009,e58d000c,e3a00008,e58d0010,e3a00002,e58d0014,e1a0000d,e3a01006,
  //   eb000000,eafffffe,e3a02000,e24dd018,e58de000,e58d1004,e1a03001,e1510002,a000014,e58d0008,
  //   e1a01003,e58d2010,e58d300c,eb000013,e3a0c004,e000009c,e1a0c000,e59d0008,e080c00c,
  //   e5901000,e59c2000,e58c1000,e5802000,e2800004,e59d1004,e59d2010,e2822001,e59d300c,
  //   e2433001,eaffffe8,e59de000,e59d0004,e28dd018,e12fff1e,e24dd004,e3a03000,e58d3000,
  //   e5902000,e2800004,e2833001,e1530001,a000005,e590c000,e152000c,aafffff8,e1a0200c,e58d3000,
  //   eafffff5,e59d0000,e28dd004,e12fff1e
endmodule
