// Digital circuit 16bit_adder.dig as structural Verilog
module _16bit_adder (
  input  cin,
  input  [15:0] a,
  input  [15:0] b,
  output cout,
  output [15:0] sum
);

  wire _4_bit_adder_1_cout, _4_bit_adder_2_cout, _4_bit_adder_3_cout;

  _4_bit_adder _4_bit_adder_1 (.cin(cin), .cout(_4_bit_adder_1_cout), .a(a[3:0]), .b(b[3:0]), .sum(sum[3:0]));
  _4_bit_adder _4_bit_adder_2 (
    .cin(_4_bit_adder_1_cout), .cout(_4_bit_adder_2_cout), .a(a[7:4]), .b(b[7:4]), .sum(sum[7:4]));
  _4_bit_adder _4_bit_adder_3 (
    .cin(_4_bit_adder_2_cout), .cout(_4_bit_adder_3_cout), .a(a[11:8]), .b(b[11:8]), .sum(sum[11:8]));
  _4_bit_adder _4_bit_adder_4 (.cin(_4_bit_adder_3_cout), .cout(cout), .a(a[15:12]), .b(b[15:12]), .sum(sum[15:12]));
endmodule
