// Digital circuit 16bit_counter.dig as structural Verilog
module _16bit_counter (
  input  CLK,
  input  CLR,
  output [15:0] COUNT
);

  wire not_1_out;
  wire [15:0] _16bit_adder_1_sum;

  not not_1 (not_1_out, CLR);
  _16bit_register _16bit_register_1 (.D(_16bit_adder_1_sum), .CLK(CLK), .CLR(not_1_out), .Q(COUNT));
  _16bit_adder _16bit_adder_1 (.cin(1'b0), .sum(_16bit_adder_1_sum), .a(COUNT), .b(16'h1));  // open: cout
endmodule
