// Digital circuit 2to1-1bit-multiplexor.dig as structural Verilog
module _2to1_1bit_multiplexor (
  input  A,
  input  B,
  input  S,
  output OUT
);

  wire and_1_out, and_2_out;

  and and_1 (and_1_out, ~S, A);  // And
  and and_2 (and_2_out, S, B);
  or or_1 (OUT, and_1_out, and_2_out);
endmodule
