// Digital circuit 4-bit-adder.dig as structural Verilog
module _4_bit_adder (
  input  cin,
  input  [3:0] a,
  input  [3:0] b,
  output cout,
  output [3:0] sum
);

  wire _1_bit_adder_1_cout, _1_bit_adder_2_cout, _1_bit_adder_3_cout;

  _1_bit_adder _1_bit_adder_1 (.a(a[0]), .b(b[0]), .cin(cin), .sum(sum[0]), .cout(_1_bit_adder_1_cout));
  _1_bit_adder _1_bit_adder_2 (.a(a[1]), .b(b[1]), .cin(_1_bit_adder_1_cout), .sum(sum[1]), .cout(_1_bit_adder_2_cout));
  _1_bit_adder _1_bit_adder_3 (.a(a[2]), .b(b[2]), .cin(_1_bit_adder_2_cout), .sum(sum[2]), .cout(_1_bit_adder_3_cout));
  _1_bit_adder _1_bit_adder_4 (.a(a[3]), .b(b[3]), .cin(_1_bit_adder_3_cout), .sum(sum[3]), .cout(cout));
endmodule
