// Digital circuit 4-bit-main.dig as structural Verilog
module _4_bit_main (
  input  [3:0] a,
  input  [3:0] b,
  input  cin,
  output cout,
  output [3:0] sum
);

  _4_bit_adder _4_bit_adder_1 (.cin(cin), .cout(cout), .a(a), .b(b), .sum(sum));
  // Probe sum-bin on sum
endmodule
