// Digital circuit 4-bit-register.dig as structural Verilog
module _4_bit_register (
  input  CLK,
  input  [3:0] D,
  input  CLR,
  output [3:0] Q
);

  D_flipflop d_flipflop_1 (.D(D[0]), .CLK(CLK), .CLR(CLR), .Q(Q[0]));  // open: not_Q
  D_flipflop d_flipflop_2 (.D(D[1]), .CLK(CLK), .CLR(CLR), .Q(Q[1]));  // open: not_Q
  D_flipflop d_flipflop_3 (.D(D[2]), .CLK(CLK), .CLR(CLR), .Q(Q[2]));  // open: not_Q
  D_flipflop d_flipflop_4 (.D(D[3]), .CLK(CLK), .CLR(CLR), .Q(Q[3]));  // open: not_Q
endmodule
