// Digital circuit 8to1-1bit-MUX.dig as structural Verilog
module _8to1_1bit_MUX (
  input  A0,
  input  A1,
  input  A2,
  input  A3,
  input  A4,
  input  A5,
  input  A6,
  input  A7,
  input  [2:0] S,
  output OUT
);

  wire _4to1_1bit_multiplexor_1_out, _4to1_1bit_multiplexor_2_out;

  _4to1_1bit_multiplexor _4to1_1bit_multiplexor_1 (
    .A0(A0), .A1(A1), .A2(A2), .A3(A3), .S(S[1:0]), .OUT(_4to1_1bit_multiplexor_1_out));
  _4to1_1bit_multiplexor _4to1_1bit_multiplexor_2 (
    .A0(A4), .A1(A5), .A2(A6), .A3(A7), .S(S[1:0]), .OUT(_4to1_1bit_multiplexor_2_out));
  _2to1_1bit_multiplexor _2to1_1bit_multiplexor_1 (
    .A(_4to1_1bit_multiplexor_1_out), .B(_4to1_1bit_multiplexor_2_out), .S(S[2]), .OUT(OUT));
endmodule
