// Digital circuit D-Latch.dig as structural Verilog
module D_Latch (
  input  CLK,
  input  D,
  input  CLR,
  output Q,
  output not_Q
);

  wire and_1_out, and_2_out, and_3_out, or_1_out;

  or or_1 (or_1_out, CLK, CLR);
  and and_1 (and_1_out, D, ~CLR);  // And
  and and_2 (and_2_out, or_1_out, ~and_1_out);  // And
  and and_3 (and_3_out, or_1_out, and_1_out);
  SR_Latch sr_latch_1 (.R(and_2_out), .S(and_3_out), .Q(Q), .notQ(not_Q));
endmodule
