// Digital circuit D-flipflop.dig as structural Verilog
module D_flipflop (
  input  D,
  input  CLK,
  input  CLR,
  output Q,
  output not_Q
);

  wire d_latch_1_q, not_1_out;

  not not_1 (not_1_out, CLK);
  D_Latch d_latch_1 (.CLK(not_1_out), .D(D), .CLR(CLR), .Q(d_latch_1_q));  // open: not_Q
  D_Latch d_latch_2 (.CLK(CLK), .D(d_latch_1_q), .CLR(CLR), .Q(Q), .not_Q(not_Q));
endmodule
