// Digital circuit ROM.dig as structural Verilog
module ROM (
  input  [4:0] ADDR,
  output [7:0] ROW
);

  ROM #(.AddrBits(5), .Bits(8)) rom_1 (.A(ADDR), .sel(1'b1), .D(ROW));

  // Notes on the sheet:
  //   contents of rom_1 (hex, n*v repeats v):
  //   0,0,3c,0,0,0,0,0,0,0,4,4,4,4,0,0,0,0,0,0,0,3c,0,0,0,0,20,20,20,20
endmodule
