// Digital circuit decoder.dig as structural Verilog
module decoder (
  input  En,
  input  [3:0] Sel,
  output Out0,
  output Out1,
  output Out2,
  output Out3,
  output Out4,
  output Out5,
  output Out6,
  output Out7,
  output Out8,
  output Out9,
  output Out10,
  output Out11,
  output Out12,
  output Out13,
  output Out14,
  output Out15
);

  wire d0, d1, d2, d3, d4, d5, d6, d7, d8, d9, d10, d11, d12, d13, d14, d15;

  Decoder #(.Selector_Bits(4)) decoder_1 (
    .sel(Sel), .out_0(d0), .out_1(d1), .out_2(d2), .out_3(d3), .out_4(d4), .out_5(d5), .out_6(d6),
    .out_7(d7), .out_8(d8), .out_9(d9), .out_10(d10), .out_11(d11), .out_12(d12), .out_13(d13), .out_14(d14),
    .out_15(d15));
  and and_1 (Out0, En, d0);
  and and_2 (Out1, En, d1);
  and and_3 (Out2, En, d2);
  and and_4 (Out3, En, d3);
  and and_5 (Out4, En, d4);
  and and_6 (Out5, En, d5);
  and and_7 (Out6, En, d6);
  and and_8 (Out7, En, d7);
  and and_9 (Out8, En, d8);
  and and_10 (Out9, En, d9);
  and and_11 (Out10, En, d10);
  and and_12 (Out11, En, d11);
  and and_13 (Out12, En, d12);
  and and_14 (Out13, En, d13);
  and and_15 (Out14, En, d14);
  and and_16 (Out15, En, d15);
endmodule
