// Digital circuit main.dig as structural Verilog
module main (
  input  CLK,
  input  [2:0] Sel
);

  wire a_mul, ALU1src, ALUop, and_1_out, BL, BR, BX, C, CMP, comparator_1_eq, dipswitch_1_out, LDR, MUL, N,
       NZCV, or_1_out, r0, r1, r2, r3, r4, r5, r6, r7, r8, r9, r10, r11, r12, r13, r14, r15, register_p8,
       RFW, STR, V, Z;
  wire [1:0] EXT;
  wire [3:0] _0_3, _8_11, _12_15, _16_19, cond, multiplexer_2_out, multiplexer_4_out, multiplexer_5_out,
       multiplexer_6_out;
  wire [23:4] b_offset;
  wire [23:20] bxcode;
  wire [31:0] add_1_s, add_2_s, D, extender_1_extimm, multiplexer_3_out, multiplexer_7_out,
       multiplexer_8_out, multiplexer_9_out, pc_in, pc_out, R, register_p25;

  DipSwitch dipswitch_1 (.out(dipswitch_1_out));
  // control control_unit: pin names not known; wires that end beside it: {cond, bxcode, b_offset[23:22], a_mul, b_offset[20], _16_19, _12_15, _8_11, b_offset[7:4], _0_3}, NZCV, CLK, RFW, EXT, ALUop, ALU1src, CMP, MUL, LDR, STR, BR, BL, BX
  and and_1 (and_1_out, CLK, dipswitch_1_out);
  Multiplexer #(.Selector_Bits(2), .Bits(32)) multiplexer_1 (
    .sel({BX, BR}), .in_0(add_1_s), .in_1(R), .in_2(register_p25), .in_3({32{1'b0}}), .out(pc_in));
  // Probe on {cond, bxcode, b_offset[23:22], a_mul, b_offset[20], _16_19, _12_15, _8_11, b_offset[7:4], _0_3}
  Register #(.Bits(32)) PC (.D(pc_in), .C(and_1_out), .en(1'b1), .Q(pc_out));
  inst_mem ROM (
    .A(pc_out[8:2]), .Sel(Sel),
    .D({cond, bxcode, b_offset[23:22], a_mul, b_offset[20], _16_19, _12_15, _8_11, b_offset[7:4], _0_3}));
  Add #(.Bits(32)) add_1 (.a(pc_out), .b(32'h4), .c_i(1'b0), .s(add_1_s));  // open: c_o
  // Probe on cond
  // Probe on cond
  // Probe on cond
  // Probe on cond
  // Probe on r0
  // Probe on r1
  // Probe on r2
  // Probe on r3
  // Probe on bxcode[23]
  // Probe on {bxcode, b_offset[23:22]}
  // Probe on bxcode[23:22]
  // Probe on bxcode[23:21]
  Multiplexer #(.Bits(4)) multiplexer_2 (.sel(MUL), .in_0(_16_19), .in_1(_8_11), .out(multiplexer_2_out));
  or or_1 (or_1_out, LDR, STR);
  Multiplexer #(.Bits(32)) multiplexer_3 (.sel(LDR), .in_0({32{1'b0}}), .in_1(D), .out(multiplexer_3_out));
  Multiplexer #(.Selector_Bits(2), .Bits(4)) multiplexer_4 (
    .sel({MUL, BL}), .in_0(_12_15), .in_1(4'b1110), .in_2(_16_19), .in_3(4'b0000), .out(multiplexer_4_out));
  // Probe on r4
  // Probe on r5
  // Probe on r6
  // Probe on r7
  // Probe on bxcode[21]
  // Probe on a_mul
  // Probe on bxcode[21]
  // Probe on bxcode[20]
  Multiplexer #(.Bits(4)) multiplexer_5 (.sel(BR), .in_0(multiplexer_2_out), .in_1(4'b1111), .out(multiplexer_5_out));
  Multiplexer #(.Bits(4)) multiplexer_6 (
    .sel(or_1_out), .in_0(_0_3), .in_1(multiplexer_4_out), .out(multiplexer_6_out));
  // Probe on r8
  // Probe on r9
  // Probe on r10
  // Probe on r11
  // Probe on {bxcode[20], b_offset[23:22], a_mul}
  // Probe on b_offset[20]
  // Probe on bxcode[20]
  // Probe on {b_offset[23:22], a_mul, b_offset[20], _16_19, _12_15, _8_11, b_offset[7:4], _0_3}
  Multiplexer #(.Selector_Bits(2), .Bits(32)) multiplexer_7 (
    .sel({LDR, BL}), .in_0(R), .in_1(add_1_s), .in_2(multiplexer_3_out), .in_3({32{1'b0}}),
    .out(multiplexer_7_out));
  Add #(.Bits(32)) add_2 (.a(add_1_s), .b(32'h4), .c_i(1'b0), .s(add_2_s));  // open: c_o
  // Probe on r12
  // Probe on r13
  // Probe on r14
  // Probe on r15
  // Probe on b_offset[20]
  // Probe on b_offset[20]
  // Probe on b_offset[23]
  // register register: pin names not known; wires that end beside it: multiplexer_5_out, multiplexer_6_out, RFW, multiplexer_4_out, multiplexer_7_out, CLK, add_2_s, register_p8, r0, r1, r2, r3, r4, r5, r6, r7, r8, r9, r10, r11, r12, r13, r14, r15, register_p25
  // Probe on _16_19
  // Probe on b_offset[22]
  // Probe on pc_out
  // Probe on pc_in
  // Probe on _16_19
  // Probe on _12_15
  // Probe on _12_15
  // Probe on a_mul
  // Probe on N
  // Probe on Z
  // Probe on C
  // Probe on V
  // Probe on _8_11
  // Probe on b_offset[20]
  // Probe on _0_3
  extender extender_1 (
    .iw({cond, bxcode, b_offset[23:22], a_mul, b_offset[20], _16_19, _12_15, _8_11, b_offset[7:4], _0_3}),
    .EXT(EXT), .extimm(extender_1_extimm));
  // Probe on b_offset[7:4]
  // Probe on _16_19
  // Probe on _0_3
  Comparator #(.Bits(32)) comparator_1 (.a(pc_in), .b(pc_out), .eq(comparator_1_eq));  // open: gt, lt
  // Probe on {b_offset[7:4], _0_3}
  LED Finish_light (.in(comparator_1_eq));
  // Probe on _0_3
  // Probe on _12_15
  // Probe on {_8_11, b_offset[7:4], _0_3}
  Multiplexer #(.Bits(32)) multiplexer_8 (
    .sel(ALU1src), .in_0(register_p25), .in_1(extender_1_extimm), .out(multiplexer_8_out));
  Multiplexer #(.Bits(32)) multiplexer_9 (
    .sel(ALU1src), .in_0(extender_1_extimm), .in_1(register_p25), .out(multiplexer_9_out));
  // alu alu_1: pin names not known; wires that end beside it: register_p8, multiplexer_8_out, ALUop, R, NZCV, N, Z, C, V
  RAMDualPort #(.AddrBits(9), .Bits(32)) ramdualport_1 (
    .A(R[10:2]), .Din(multiplexer_9_out), .str(STR), .C(CLK), .ld(LDR), .D(D));

  // Other names for the same wires on the sheet: b_offset (some bits) = {a_mul, _16_19, _12_15, _8_11, _0_3};
  //   imm[7:0] = {b_offset[7:4], _0_3}; immoff[11:0] = {_8_11, b_offset[7:4], _0_3};
  //   iw[31:0] = {cond, bxcode, b_offset[23:22], a_mul, b_offset[20], _16_19, _12_15, _8_11, b_offset[7:4], _0_3};
  //   rm[3:0] = _0_3; rm_mul[3:0] = _0_3;
  //   bxcode[19:0] = {b_offset[23:22], a_mul, b_offset[20], _16_19, _12_15, _8_11, b_offset[7:4]};
  //   opmul4[3:0] = b_offset[7:4]; rs_mul[3:0] = _8_11; rd[3:0] = _12_15; rn_mul[3:0] = _12_15; rd_mul[3:0] = _16_19;
  //   rn[3:0] = _16_19; l_sdt = b_offset[20]; s_dp = b_offset[20]; s_mul = b_offset[20];
  //   opc[3:0] = {bxcode[20], b_offset[23:22], a_mul}; w_sdt = a_mul; b_sdt = b_offset[22];
  //   opmul6[5:0] = {bxcode, b_offset[23:22]}; u_sdt = b_offset[23]; l_b = bxcode[20]; p_sdt = bxcode[20];
  //   i_sdt = bxcode[21]; op0_i_dp = bxcode[21]; opb3[2:0] = bxcode[23:21]; op1 = bxcode[22];
  //   opmul2[1:0] = bxcode[23:22]; op2 = bxcode[23]

  // Notes on the sheet:
  //   CLK: Hz: 20
  //   0: Quadratic
  //   x = 2, a = 3, b = 4, c = 5
  //   25
  //   1: Sum array
  //   {1, 2, 3, 4, 6}
  //   16
  //   2: Find max.
  //   {3, 6, 1, 8, 4}
  //   8
  //   3: fib iter 10.
  //   n = 10
  //   55
  //   4: fib iter 19.
  //   n = 19
  //   4181
  //   5: fib rec 10
  //   n = 10.
  //   55
  //   6: fib rec 19.
  //   n = 19
  //   4181
  //   7: sort
  //   {1, 4, 7, 9, 8, 2}
  //   len = 6
  //   return:
  //   {9, 8, 7, 4, 2, 1}
  //   B
  //   DP
  //   MUL
  //   SDT
endmodule
