// Digital circuit 16bit_register.dig as structural Verilog
module _16bit_register (
  input  [15:0] D,
  input  CLK,
  input  CLR,
  output [15:0] Q
);

  _4_bit_register _4_bit_register_1 (.CLK(CLK), .D(D[3:0]), .CLR(CLR), .Q(Q[3:0]));
  _4_bit_register _4_bit_register_2 (.CLK(CLK), .D(D[7:4]), .CLR(CLR), .Q(Q[7:4]));
  _4_bit_register _4_bit_register_3 (.CLK(CLK), .D(D[11:8]), .CLR(CLR), .Q(Q[11:8]));
  _4_bit_register _4_bit_register_4 (.CLK(CLK), .D(D[15:12]), .CLR(CLR), .Q(Q[15:12]));
endmodule
