// Digital circuit 4to1-1bit-multiplexor.dig as structural Verilog
module _4to1_1bit_multiplexor (
  input  A0,
  input  A1,
  input  A2,
  input  A3,
  input  [1:0] S,
  output OUT
);

  wire _2to1_1bit_multiplexor_1_out, _2to1_1bit_multiplexor_2_out;

  _2to1_1bit_multiplexor _2to1_1bit_multiplexor_1 (.A(A0), .B(A1), .S(S[0]), .OUT(_2to1_1bit_multiplexor_1_out));
  _2to1_1bit_multiplexor _2to1_1bit_multiplexor_2 (.A(A2), .B(A3), .S(S[0]), .OUT(_2to1_1bit_multiplexor_2_out));
  _2to1_1bit_multiplexor _2to1_1bit_multiplexor_3 (
    .A(_2to1_1bit_multiplexor_1_out), .B(_2to1_1bit_multiplexor_2_out), .S(S[1]), .OUT(OUT));
endmodule
