// Digital circuit Control.dig as structural Verilog
module Control (
  input  [15:0] COUNT,
  output BUFSEL,
  output [6:0] RAM_ADDR,
  output [2:0] S,
  output [4:0] ROM_ADDR
);

  not not_1 (BUFSEL, COUNT[6]);

  assign RAM_ADDR = COUNT[6:0];
  assign ROM_ADDR = COUNT[7:3];
  assign S = COUNT[2:0];
endmodule
