// Digital circuit Final.dig as structural Verilog
module Final (
  input  CLK
);

  wire _8to1_1bit_mux_1_out, control_1_bufsel, dipswitch_1_out;
  wire [2:0] control_1_s;
  wire [4:0] control_1_rom_addr;
  wire [6:0] control_1_ram_addr;
  wire [7:0] rom_1_row;
  wire [15:0] _16bit_counter_1_p3;

  DipSwitch dipswitch_1 (.out(dipswitch_1_out));
  // _16bit_counter _16bit_counter_1: pin names not known; wires that end beside it: CLK, dipswitch_1_out, _16bit_counter_1_p3
  Control control_1 (
    .COUNT(_16bit_counter_1_p3), .S(control_1_s), .ROM_ADDR(control_1_rom_addr),
    .RAM_ADDR(control_1_ram_addr), .BUFSEL(control_1_bufsel));
  ROM rom_1 (.ROW(rom_1_row), .ADDR(control_1_rom_addr));
  _8to1_1bit_MUX _8to1_1bit_mux_1 (
    .A0(rom_1_row[0]), .A1(rom_1_row[1]), .A2(rom_1_row[2]), .A3(rom_1_row[3]), .A4(rom_1_row[4]),
    .A5(rom_1_row[5]), .A6(rom_1_row[6]), .A7(rom_1_row[7]), .S(control_1_s), .OUT(_8to1_1bit_mux_1_out));
  RAM ram_1 (.PIXEL(_8to1_1bit_mux_1_out), .ADDR(control_1_ram_addr), .CLK(CLK), .BUFSEL(control_1_bufsel));

  // Notes on the sheet:
  //   CLK: Hz: 64
endmodule
