// Digital circuit RAM.dig as structural Verilog
module RAM (
  input  [6:0] ADDR,
  input  BUFSEL,
  input  CLK,
  input  PIXEL
);

  GraphicCard #(.graphicHeight(8), .graphicWidth(8)) Display (
    .A(ADDR), .str(1'b1), .C(CLK), .ld(1'b0), .B(BUFSEL), .D(PIXEL));
endmodule
